# Fritzing sketch ESPHome-Multisensor_WROOM32 (saved by Fritzing 0.9.10b)

parts:
  Mod1 = SDS011_1 [part_number=1]
  TD-er1 = MH-Z19 CO2 sensor [part_number=MH-Z19]
  RHT2 = Humidity and Temperature Sensor RHT03 [part_number=DHT22]
  U2 = ESP32-38PinWide [part_number=ESP32-38PinWide]

nets:
  N1: Mod1.connector2, U2.VIN
  GND: Mod1.connector4, TD-er1.GND, RHT2.GND_2, U2.GND
  N2: Mod1.connector5, U2.GPIO1
  N3: Mod1.connector6, U2.GPIO3
  N4: TD-er1.RX, U2.GPIO17
  N5: TD-er1.TX, U2.GPIO16
  N6: TD-er1.Vin, U2.3.3
  N7: RHT2.Data-signal, U2.GPIO27

custom parts:
  ESP32-38PinWide: Generic 38-Pin ESP32 with wide format (only access to one side of pins on a breadboard) based on Stephen Lilley's HiLetgo ESP-WROOM-32 ESP32 ESP-32S Development Board.
